# Fritzing sketch 12 FINAL-PROJECT (CAPACITANCE) (saved by Fritzing 0.9.3b)
breadboards: 1

parts:
  Part1 = Arduino Mega 2560 (Rev3)
  R1 = Resistor [tolerance=±5% resistance=10k package=THT]
  R2 = Resistor [tolerance=±5% resistance=220 package=THT]
  C1 = Tantalum Capacitor [capacitance=1μF package="100 mil [THT, tantalum]"]

nets:
  N1: Part1.A0, R1.Pin_1, R2.Pin_0, C1.+
  N2: Part1.GND, C1.-
  N3: Part1.D13_PWM, R1.Pin_0
  N4: Part1.D11_PWM, R2.Pin_1

notes:
  Capacitance Meter for 1uF to 3.9 uF capacitors using Arduino Mega (REV3)
  ARANO-VERTULFO
  Final Term Project
  1 unknown Capacitor
  1 10k ohms Resistor
  1 220 ohms Resistor
