# Fritzing sketch FINAL-PROJECT (INDUCTANCE) (saved by Fritzing 0.9.3b)
breadboards: 1

parts:
  Part1 = Arduino Nano (Rev3.0)
  R1 = Resistor [tolerance=±5% resistance=150 package=THT]
  D1 = Rectifier Diode [part_number=1N4001 package="300 mil [THT]"]
  L4 = Inductor [package="0805 [SMD]"]
  U2 = IC, DIP package, 14 pins [chip_label=IC]
  C1 = Tantalum Capacitor [capacitance=1μF package="100 mil [THT, tantalum]"]
  C2 = Tantalum Capacitor [capacitance=1μF package="100 mil [THT, tantalum]"]
  R2 = Resistor [tolerance=±5% resistance=330 package=THT]
  LCD1 = LCD screen  # not connected

nets:
  N1: Part1.GND, L4.pin_1, U2.pin5, U2.pin13, C1.-, C2.+
  N2: Part1.D11/MOSI, U2.pin8, R2.Pin_0
  N3: Part1.5V, U2.pin10, R2.Pin_1
  N4: Part1.D13/SCK, R1.Pin_0
  N5: R1.Pin_1, D1.cathode
  N6: D1.anode, L4.pin_0, U2.pin14, C1.+, C2.-

notes:
  SCL
  SDA
  5V
  GND
  ARANO-VERTULFO
  Final Term Project
  Inductance Meter using Arduino Nano (v3.0)
  LM339 Comparator
  2 1uF capacitor (nonpolar)
  1 150 ohms Resistor
  1 330 ohms Resistor
  1 diode (1n4001)
  1 LCD with i2c
