# Fritzing sketch MIDTERM FRITZING FILE (saved by Fritzing 0.9.3b)
breadboards: 1

parts:
  Part1 = Arduino Mega 2560 (Rev3)
  R1 = Resistor [tolerance=±5% resistance=330 package=THT]
  R2 = Resistor [tolerance=±5% resistance=220 package=THT]
  R3 = Resistor [tolerance=±5% resistance=470 package=THT]
  R4 = Resistor [tolerance=±5% resistance=1k package=THT]
  R5 = Resistor [tolerance=±5% resistance=1k package=THT]
  R6 = Resistor [tolerance=±5% resistance=1k package=THT]

nets:
  N1: Part1.A2, R3.Pin_0, R6.Pin_1
  N2: Part1.A3, R2.Pin_0, R5.Pin_1
  N3: Part1.A4, R1.Pin_0, R4.Pin_1
  N4: Part1.5V, R4.Pin_0, R5.Pin_0, R6.Pin_0
  N5: Part1.GND, R1.Pin_1, R2.Pin_1, R3.Pin_1

notes:
  330 ohms
  220 ohms
  470 ohms
  ARDUINO MEGA 2560
  DELTA TO WYE TRANSFORMATION
  1000 ohms
  1000 ohms
  1000 ohms

// code stored in the sketch: DELTA-Y_TRANSFORMATION.ino
const int sensorPin1 = A2; 
const int sensorPin2 = A3;
const int sensorPin3 = A4;
int sensorValue1 = 0;   
int sensorValue2 = 0;
int sensorValue3 = 0;
float Vin = 5;
float Vout1 = 0;  
float Vout2 = 0;
float Vout3 = 0;
float Rref1 = 1000; 
float Rref2 = 1000;
float Rref3 = 1000;
float r1 = 0; 
float r2 = 0;  
float r3 = 0;
float rA=0,rB=0,rC=0;
void setup ()
{
  Serial.begin(9600);      // Initialize serial communications at 9600 bps
}
void getR1(){
  sensorValue1 = analogRead(sensorPin1);
  Vout1 = (Vin * sensorValue1) / 1023;    
  r1 = Rref1 * (1 / ((Vin / Vout1) - 1));  
  Serial.print("Resistor 1: ");                  
  Serial.println(r1);                
  delay(1000);
  }
  void getR2(){
  sensorValue2 = analogRead(sensorPin2);
  Vout2 = (Vin * sensorValue2) / 1024;    
  r2 = Rref2 * (1 / ((Vin / Vout2) - 1));  
  Serial.print("Resistor 2: ");                  
  Serial.println(r2);                     // Give calculated resistance in Serial Monitor
  delay(1000);
  }
  void getR3(){
  sensorValue3 = analogRead(sensorPin3);
  Vout3 = (Vin * sensorValue3) / 1024;    
  r3 = Rref3 * (1 / ((Vin / Vout3) - 1));  
  Serial.print("Resistor 3: ");                  
  Serial.println(r3);                     // Give calculated resistance in Serial Monitor
    delay(1000);
  }
void loop ()
{
  Serial.println("******************************************");
  Serial.println("*******Delta to Y Transformation**********");
  Serial.println("-DELTA RESISTOR'S VALUE-");
  getR1();
  getR2();
  getR3();
  Serial.println("-Y RESISTOR'S VALUE-");
  delay(2000);
   rA=(r2*r3)/(r1+r2+r3);
   rB=(r3*r1)/(r1+r2+r3);
    rC=(r1*r2)/(r1+r2+r3);
    Serial.print("Resistor A:");
    Serial.println(rA);
    Serial.print("Resistor B:");
    Serial.println(rB);
    Serial.print("Resistor C:");
    Serial.println(rC);
    Serial.println("********************************************");
delay(2000);
}
